# Fritzing sketch Electrical Drawings (saved by Fritzing 0.9.3b)
breadboards: 1

parts:
  Part1 = Arduino Mega ADK (Rev3)
  Left = hc-sr04
  Back = hc-sr04
  Right = hc-sr04
  Down = hc-sr04
  Front = hc-sr04
  Part2 = Bluetooth Mate Silver
  Part3 = Arduino Nano (Rev3.0)
  R3 = Resistor [tolerance=±5% resistance=220 package="0603 [SMD]"]
  IR_Module = Gas Sensor Breakout Board
  LED1 = smd LED [color="Red (633nm)" package="0603 [SMD]"]
  LED2 = smd LED [color="Red (633nm)" package="0603 [SMD]"]
  LED3 = smd LED [color="Red (633nm)" package="0603 [SMD]"]
  LED5 = smd LED [color="Red (633nm)" package="0603 [SMD]"]
  LED6 = smd LED [color="Red (633nm)" package="0603 [SMD]"]
  LED7 = smd LED [color="Red (633nm)" package="0603 [SMD]"]
  R9 = Resistor [tolerance=±5% resistance=220 package="0603 [SMD]"]  # not connected
  R10 = Resistor [tolerance=±5% resistance=220 package="0603 [SMD]"]
  R11 = Resistor [tolerance=±5% resistance=220 package="0603 [SMD]"]
  R12 = Resistor [tolerance=±5% resistance=220 package="0603 [SMD]"]
  R13 = Resistor [tolerance=±5% resistance=220 package="0603 [SMD]"]
  R14 = Resistor [tolerance=±5% resistance=220 package="0603 [SMD]"]
  R15 = Resistor [tolerance=±5% resistance=220 package="0603 [SMD]"]
  LED8 = smd LED [color="Red (633nm)" package="0603 [SMD]"]
  LED9 = smd LED [color="Red (633nm)" package="0603 [SMD]"]
  Part4 = Shift Register Breakout - 74HC595
  Part5 = Compass Module - HMC6352
  BAT1 = Battery Holders [package=battery-aaa]

nets:
  N1: Part1.A0, Part3.A1
  N2: Part1.A1, Part3.A0
  N3: Part1.D21/SCL, Part5.SCL
  N4: Part1.D20/SDA, Part5.SDA
  GND: Part1.GND, Left.GND, Back.GND, Right.GND, Down.GND, Front.GND, Part2.GND, Part3.GND, R3.Pin_1, R10.Pin_1, R11.Pin_1, R12.Pin_1, R13.Pin_1, R14.Pin_1, R15.Pin_1, Part4.GND, Part5.GND
  VCC: Part1.VIN, Part1.D39, Left.VCC, Back.VCC, Right.VCC, Down.VCC, Front.VCC, Part2.VCC, Part3.VIN, Part4.VCC, Part5.VCC, BAT1.-, BAT1.+
  N5: Part1.D22, IR_Module.A1
  N6: Part1.D23, IR_Module.B1
  N7: Part1.D24, IR_Module.H1
  N8: Part1.D25, IR_Module.GND
  N9: Part1.D28, Part4.LATCH_CLOCK
  N10: Part1.D29, Part4.SERIAL_IN
  N11: Part1.D30, Part4.CLOCK
  N12: Part1.D40, Front.Trig
  N13: Part1.D41, Front.Echo
  N14: Part1.D42, Down.Trig
  N15: Part1.D43, Down.Echo
  N16: Part1.D44, Right.Trig
  N17: Part1.D45, Right.Echo
  N18: Part1.D46, Left.Trig
  N19: Part1.D47, Left.Echo
  N20: Part1.D48, Back.Trig
  N21: Part1.D49, Back.Echo
  N22: Part1.D50/MISO, Part2.RX_5V
  N23: Part1.D51/MOSI, Part2.TX_5V
  N24: R3.Pin_0, LED5.anode
  N25: LED1.cathode, Part4.QE
  N26: LED1.anode, R12.Pin_0
  N27: LED2.cathode, Part4.QF
  N28: LED2.anode, R13.Pin_0
  N29: LED3.cathode, Part4.QD
  N30: LED3.anode, R11.Pin_0
  N31: LED5.cathode, Part4.QA
  N32: LED6.cathode, Part4.QB
  N33: LED7.cathode, Part4.QC
  N34: LED7.anode, R10.Pin_0
  N35: R14.Pin_0, LED9.anode
  N36: R15.Pin_0, LED8.anode
  N37: LED8.cathode, Part4.QG
  N38: LED9.cathode, Part4.QH
